# Fritzing sketch krishi_mitra (saved by Fritzing 0.9.3b)
breadboards: 1

parts:
  B1 = Bolt WiFi Module [package=dip]
  Part1 = ESP-WROOM-32 [ESP-32S] Module [part_number=ESP-WROOM-32]
  Part2 = Soil Moisture Sensor
  Part3 = Logic Level Converter
  OMRON1 = OMRON PCB Power Relay – G5LE [part_number="G5LE-1\n" package=THT]
  M1 = DC Motor
  BAT1 = BC9VPC [package=bc9vpc]
  BAT2 = BC9VPC [package=bc9vpc]
  PIR1 = PIR sensor

nets:
  GND: B1.pin1, Part1.GND, Part2.GND, Part3.GND, OMRON1.COIL1, M1.pin_2, BAT2.V-
  N1: B1.pin2, PIR1.SIG
  N2: B1.pin8, Part1.IO16
  N3: B1.pin10, Part3.LV
  VCC: B1.pin11, Part2.VCC, Part3.HV, PIR1.VDD
  N4: Part1.IO2, Part3.TX_HV
  N5: Part3.RX_LV, OMRON1.COIL2
  N6: OMRON1.C, BAT1.V+
  N7: OMRON1.B, M1.pin_1
  N8: BAT1.V-, BAT2.V+

custom parts:
  Bolt WiFi Module: Bolt IoT platform gives you the capability to control your devices and collect data from IoT devices safely and securely no matter where you are. Get actionable insights by deploying machine learning algorithms with just a few clicks to detect anomalies as well as predict sensor values.
  ESP-WROOM-32 [ESP-32S] Module: Espressif ESP-WROOM-32 WiFi/Bluetooth LE microcontroller module also known as the Ai-Thinker ESP-32S module with similar formfactor. The ESP32 is a microcontroller chip with WiFi and BLE capabilities. The chip is developed by Espressif and is the successor to the popular ESP8266 WiFi module.
